# Fritzing sketch Simon-Fritzing (saved by Fritzing 0.8.5b)
breadboards: 1

parts:
  Parte1 = Arduino Uno (Rev3)
  U1 = LCD-16X2 [package=lcd-16x2]
  LED2 = LED - 5mm [color="Red (633nm)" package="5 mm [THT]"]
  LED7 = LED - 5mm [color="Red (633nm)" package="5 mm [THT]"]
  LED8 = LED - 5mm [color="Red (633nm)" package="5 mm [THT]"]
  LED9 = LED - 5mm [color="Red (633nm)" package="5 mm [THT]"]
  S6 = Pushbutton [package="[THT]"]
  S7 = Pushbutton [package="[THT]"]
  S8 = Pushbutton [package="[THT]"]
  S9 = Pushbutton [package="[THT]"]
  S10 = Pushbutton [package="[THT]"]
  LED10 = LED - 5mm [color="Red (633nm)" package="5 mm [THT]"]

nets:
  N1: Parte1.D8, LED7.anode
  N2: Parte1.D9_PWM, LED8.anode
  N3: Parte1.D10_PWM/SS, LED9.anode
  N4: Parte1.D11_PWM/MOSI, LED2.anode
  N5: Parte1.D12/MISO, LED10.anode
  GND: Parte1.GND, U1.VSS, LED2.cathode, LED7.cathode, LED8.cathode, LED9.cathode, S6.Pin_1, S6.Pin_2, S7.Pin_1, S7.Pin_2, S8.Pin_1, S8.Pin_2, S9.Pin_1, S9.Pin_2, S10.Pin_1, S10.Pin_2, LED10.cathode
  N6: Parte1.D2, S6.Pin_3, S6.Pin_4
  N7: Parte1.D3_PWM, S7.Pin_3, S7.Pin_4
  N8: Parte1.D4, S8.Pin_3, S8.Pin_4
  N9: Parte1.D5_PWM, S9.Pin_3, S9.Pin_4
  N10: Parte1.D6_PWM, S10.Pin_3, S10.Pin_4
  N11: Parte1.D7, U1.R_W
  5V: Parte1.5V, U1.VDD
